# Fritzing sketch TestSketch (saved by Fritzing 0.9.3b)
breadboards: 1

parts:
  Raspberry_Pi_1 = Raspberry Pi 3 [part_number=RPI-3-V1.2]
  Pololu_A1 = Pololu A4988 [package=SO16]
  M1 = Stepper Motor - Bipolar
  J1 = Power Jack [package=power_jack_smd]
  C1 = Capacitor Polarized [package=panasonic_d]
  LED1 = LED - 5mm [color="Red (633nm)" package="5 mm [THT]"]
  LED2 = LED - 5mm [color="Red (633nm)" package="5 mm [THT]"]
  J2 = Basic Servo
  J3 = Basic Servo

nets:
  N1: Raspberry_Pi_1.GPIO2, Pololu_A1.STEP
  N2: Raspberry_Pi_1.GPIO3, Pololu_A1.DIR
  N3: Raspberry_Pi_1.GIPO4, J2.pulse
  GND: Raspberry_Pi_1.GND, Pololu_A1.GND#8, LED1.cathode, LED2.cathode, J3.gnd
  N4: Raspberry_Pi_1.GIPO17, J3.pulse
  N5: Raspberry_Pi_1.GIPO27, LED2.anode
  N6: Raspberry_Pi_1.GIPO22, LED1.anode
  5V: Raspberry_Pi_1.5V, Pololu_A1.MS1, Pololu_A1.MS2, Pololu_A1.MS3, Pololu_A1.VDD, J3.vcc
  N7: Pololu_A1.RESET, Pololu_A1.SLEEP
  N8: Pololu_A1.1B, M1.D
  N9: Pololu_A1.1A, M1.B
  N10: Pololu_A1.2A, M1.C
  N11: Pololu_A1.2B, M1.A
  N12: Pololu_A1.GND#14, J1.GND, C1.-
  N13: Pololu_A1.VMOT, J1.PWR, C1.+
